// Digital circuit 74181_74182_dual_ic.dig as structural Verilog
module _74181_74182_dual_ic (
  input  [7:0] A__7_0,
  input  [7:0] B__7_0,
  input  [3:0] S__3_0,
  input  nMath_Logic,
  input  nC_in,
  input  L_nH,
  input  [15:0] X__15_0,
  output [3:0] Result_a,
  output [3:0] nResult_b__7_4,
  output [7:0] Result__8_0,
  output [3:0] nResult_a_3_0,
  output [3:0] Result_b,
  output C_out,
  output [7:0] Result_sdec,
  output [15:0] out_14
);

  wire _74182_1_pin1, _74182_1_pin2, _74182_1_pin3, _74182_1_pin4, _74182_1_pin12;
  wire [3:0] bitextender_2_out;
  wire [7:0] bitextender_1_out, xor_1_out, xor_2_out;

  BitExtender #(.inputBits(1), .outputBits(8)) bitextender_1 (.in(L_nH), .out(bitextender_1_out));
  assign xor_1_out = A__7_0 ^ bitextender_1_out;  // XOr xor_1, 8 bits wide
  BitExtender #(.inputBits(1), .outputBits(4)) bitextender_2 (.in(L_nH), .out(bitextender_2_out));
  assign xor_2_out = bitextender_1_out ^ B__7_0;  // XOr xor_2, 8 bits wide
  assign out_14 = ~X__15_0;  // Not not_1, 16 bits wide
  _74181 _74181_1 (
    .pin1(xor_2_out[0]), .pin2(xor_1_out[0]), .pin3(S__3_0[3]), .pin4(S__3_0[2]), .pin5(S__3_0[1]),
    .pin6(S__3_0[0]), .pin7(nC_in), .pin8(nMath_Logic), .pin9(nResult_a_3_0[0]), .pin10(nResult_a_3_0[1]),
    .pin11(nResult_a_3_0[2]), .pin12(1'b0));  // open: pin13, pin14, pin15, pin16, pin17, pin18, pin19, pin20, pin21, pin22, pin23, pin24
  assign Result__8_0[3:0] = bitextender_2_out ^ nResult_a_3_0;  // XOr xor_3, 4 bits wide
  _74182 _74182_1 (
    .pin1(_74182_1_pin1), .pin2(_74182_1_pin2), .pin3(_74182_1_pin3), .pin4(_74182_1_pin4), .pin5(1'b0),
    .pin6(1'b1), .pin8(1'b0), .pin11(C_out), .pin12(_74182_1_pin12), .pin13(nC_in), .pin14(1'b0),
    .pin15(1'b1), .pin16(1'b1));  // open: pin7, pin9, pin10
  _74181 _74181_2 (
    .pin1(xor_2_out[4]), .pin2(xor_1_out[4]), .pin3(S__3_0[3]), .pin4(S__3_0[2]), .pin5(S__3_0[1]),
    .pin6(S__3_0[0]), .pin7(_74182_1_pin12), .pin8(nMath_Logic), .pin9(nResult_b__7_4[0]),
    .pin10(nResult_b__7_4[1]), .pin11(nResult_b__7_4[2]), .pin12(1'b0));  // open: pin13, pin14, pin15, pin16, pin17, pin18, pin19, pin20, pin21, pin22, pin23, pin24
  assign Result__8_0[7:4] = bitextender_2_out ^ nResult_b__7_4;  // XOr xor_4, 4 bits wide

  assign Result_a = Result__8_0[3:0];
  assign Result_b = Result__8_0[7:4];
  assign Result_sdec = Result__8_0;

  // Notes on the sheet:
  //   A__7_0: default 7
  //   B__7_0: default 3
  //   nMath_Logic: default 1
  //   nC_in: default 1
  //   X__15_0: default 7
endmodule
