// Digital circuit Adder_74182.dig as structural Verilog
module Adder_74182 (
  input  C_in,
  input  [15:0] B,
  input  [15:0] A,
  output [3:0] Sum__3_0,
  output [3:0] Sum__7_4,
  output [3:0] Sum__11_8,
  output [3:0] Sum__15_12,
  output [16:0] Sum__16_0,
  output nG,
  output nP,
  output C_out
);

  wire _74182_1_pin9, _74182_1_pin11, _74182_1_pin12, u_fulladd4_2_cout, u_fulladd4_2_gg, u_fulladd4_2_gp,
       u_fulladd4_3_cout, u_fulladd4_3_gg, u_fulladd4_3_gp, u_fulladd4_4_gg, u_fulladd4_4_gp,
       u_fulladd4_cout, u_fulladd4_gg, u_fulladd4_gp;

  fulladd4 #(.applicationType("IVERILOG")) u_fulladd4 (
    .Cin(C_in), .a(A[3:0]), .b(B[3:0]), .sum(Sum__3_0), .Cout(u_fulladd4_cout), .GP(u_fulladd4_gp),
    .GG(u_fulladd4_gg));
  fulladd4 #(.applicationType("IVERILOG")) u_fulladd4_2 (
    .Cin(_74182_1_pin12), .a(A[7:4]), .b(B[7:4]), .sum(Sum__7_4), .Cout(u_fulladd4_2_cout),
    .GP(u_fulladd4_2_gp), .GG(u_fulladd4_2_gg));
  fulladd4 #(.applicationType("IVERILOG")) u_fulladd4_3 (
    .Cin(_74182_1_pin11), .a(A[11:8]), .b(B[11:8]), .sum(Sum__11_8), .Cout(u_fulladd4_3_cout),
    .GP(u_fulladd4_3_gp), .GG(u_fulladd4_3_gg));
  fulladd4 #(.applicationType("IVERILOG")) u_fulladd4_4 (
    .Cin(_74182_1_pin9), .a(A[15:12]), .b(B[15:12]), .sum(Sum__15_12), .Cout(C_out), .GP(u_fulladd4_4_gp),
    .GG(u_fulladd4_4_gg));
  LED led_1 (.in(u_fulladd4_cout));
  LED led_2 (.in(u_fulladd4_2_cout));
  LED led_3 (.in(u_fulladd4_3_cout));
  _74182 _74182_1 (
    .pin1(u_fulladd4_2_gg), .pin2(u_fulladd4_2_gp), .pin3(u_fulladd4_gg), .pin4(u_fulladd4_gp),
    .pin5(u_fulladd4_4_gg), .pin6(u_fulladd4_4_gp), .pin7(nP), .pin8(1'b0), .pin9(_74182_1_pin9), .pin10(nG),
    .pin11(_74182_1_pin11), .pin12(_74182_1_pin12), .pin13(C_in), .pin14(u_fulladd4_3_gg),
    .pin15(u_fulladd4_3_gp), .pin16(1'b1));

  assign Sum__16_0 = {C_out, Sum__15_12, Sum__11_8, Sum__7_4, Sum__3_0};

  // Notes on the sheet:
  //   P_0
  //   G_0
  //   P_1
  //   G_1
  //   P_3
  //   G_3
  //   P_2
  //   G_2
endmodule

/* Code of fulladd4:
module fulladd4(
    input Cin,
    input [3:0] a, b,
    output [3:0] sum,
    output Cout,
    output wire GP, GG
);
    wire [3:0] p, g;
    wire [4:0] c; // Изменено на [4:0] для включения Cin

    assign p = a ^ b;
    assign g = a & b;

    assign c[0] = Cin;
    genvar i;
        generate
            for (i = 0; i < 4; i = i + 1) begin : carry_gen
                assign c[i+1] = g[i] | (p[i] & c[i]);
            end
        endgenerate

    assign sum = p ^ c[3:0];
    assign Cout = c[4];

    // Групповые сигналы Propagate и Generate для всего блока
    assign GP = ~(&p);
    assign GG = ~(g[3] | (p[3] & g[2]) | (p[3] & p[2] & g[1]) | (p[3] & p[2] & p[1] & g[0]));

endmodule
*/

/* Code of fulladd4:
module fulladd4(
    input Cin,
    input [3:0] a, b,
    output [3:0] sum,
    output Cout,
    output wire GP, GG
);
    wire [3:0] p, g;
    wire [4:0] c; // Изменено на [4:0] для включения Cin

    assign p = a ^ b;
    assign g = a & b;

    assign c[0] = Cin;
    genvar i;
        generate
            for (i = 0; i < 4; i = i + 1) begin : carry_gen
                assign c[i+1] = g[i] | (p[i] & c[i]);
            end
        endgenerate

    assign sum = p ^ c[3:0];
    assign Cout = c[4];

    // Групповые сигналы Propagate и Generate для всего блока
    assign GP = ~(&p);
    assign GG = ~(g[3] | (p[3] & g[2]) | (p[3] & p[2] & g[1]) | (p[3] & p[2] & p[1] & g[0]));
endmodule
*/

/* Code of fulladd4:
module fulladd4(
    input Cin,
    input [3:0] a, b,
    output [3:0] sum,
    output Cout,
    output wire GP, GG
);
    wire [3:0] p, g;
    wire [4:0] c; // Изменено на [4:0] для включения Cin

    assign p = a ^ b;
    assign g = a & b;

    assign c[0] = Cin;
    genvar i;
        generate
            for (i = 0; i < 4; i = i + 1) begin : carry_gen
                assign c[i+1] = g[i] | (p[i] & c[i]);
            end
        endgenerate

    assign sum = p ^ c[3:0];
    assign Cout = c[4];

    // Групповые сигналы Propagate и Generate для всего блока
     assign GP = ~(&p);
    assign GG = ~(g[3] | (p[3] & g[2]) | (p[3] & p[2] & g[1]) | (p[3] & p[2] & p[1] & g[0]));
endmodule
*/
