// Digital circuit Adder_verilog_74182.dig as structural Verilog
module Adder_verilog_74182 (
  input  C_in,
  input  [15:0] B__3_0,
  input  [15:0] A__3_0,
  output [3:0] Sum__3_0,
  output [3:0] Sum__7_4,
  output [3:0] Sum__11_8,
  output [3:0] Sum__15_12,
  output [16:0] Summ__16_0,
  output nG,
  output nP,
  output [16:0] C_out
);

  wire u_cla_ic_74182b_cnx, u_cla_ic_74182b_cny, u_cla_ic_74182b_cnz;
  wire [3:0] u_fulladd4_4_gg, u_fulladd4_4_gp;

  fulladd4 #(.applicationType("IVERILOG")) u_fulladd4 (
    .Cin(C_in), .a(A__3_0[3:0]), .b(B__3_0[3:0]), .sum(Sum__3_0), .GP(u_fulladd4_4_gp[0]),
    .GG(u_fulladd4_4_gg[0]));  // open: Cout
  fulladd4 #(.applicationType("IVERILOG")) u_fulladd4_2 (
    .Cin(u_cla_ic_74182b_cnx), .a(A__3_0[7:4]), .b(B__3_0[7:4]), .sum(Sum__7_4), .GP(u_fulladd4_4_gp[1]),
    .GG(u_fulladd4_4_gg[1]));  // open: Cout
  fulladd4 #(.applicationType("IVERILOG")) u_fulladd4_3 (
    .Cin(u_cla_ic_74182b_cny), .a(A__3_0[11:8]), .b(B__3_0[11:8]), .sum(Sum__11_8), .GP(u_fulladd4_4_gp[2]),
    .GG(u_fulladd4_4_gg[2]));  // open: Cout
  fulladd4 #(.applicationType("IVERILOG")) u_fulladd4_4 (
    .Cin(u_cla_ic_74182b_cnz), .a(A__3_0[15:12]), .b(B__3_0[15:12]), .sum(Sum__15_12), .Cout(C_out[0]),
    .GP(u_fulladd4_4_gp[3]), .GG(u_fulladd4_4_gg[3]));
  cla_ic_74182b #(.applicationType("IVERILOG")) u_cla_ic_74182b (
    .PB(u_fulladd4_4_gp), .GB(u_fulladd4_4_gg), .Cn(C_in), .PBo(nG), .GBo(nP), .Cnx(u_cla_ic_74182b_cnx),
    .Cny(u_cla_ic_74182b_cny), .Cnz(u_cla_ic_74182b_cnz));
  // Pins of 1 and 17 bits meet at C_out

  assign Summ__16_0 = {C_out[0], Sum__15_12, Sum__11_8, Sum__7_4, Sum__3_0};
endmodule

/* Code of fulladd4:
module fulladd4(
    input Cin,
    input [3:0] a, b,
    output [3:0] sum,
    output Cout,
    output wire GP, GG
);
    wire [3:0] p, g;
    wire [4:0] c; // Изменено на [4:0] для включения Cin

    assign p = a ^ b;
    assign g = a & b;

    assign c[0] = Cin;
    genvar i;
        generate
            for (i = 0; i < 4; i = i + 1) begin : carry_gen
                assign c[i+1] = g[i] | (p[i] & c[i]);
            end
        endgenerate

    assign sum = p ^ c[3:0];
    assign Cout = c[4];

    // Групповые сигналы Propagate и Generate для всего блока
    assign GP = ~(&p);
    assign GG = ~(g[3] | (p[3] & g[2]) | (p[3] & p[2] & g[1]) | (p[3] & p[2] & p[1] & g[0]));

endmodule
*/

/* Code of fulladd4:
module fulladd4(
    input Cin,
    input [3:0] a, b,
    output [3:0] sum,
    output Cout,
    output wire GP, GG
);
    wire [3:0] p, g;
    wire [4:0] c; // Изменено на [4:0] для включения Cin

    assign p = a ^ b;
    assign g = a & b;

    assign c[0] = Cin;
    genvar i;
        generate
            for (i = 0; i < 4; i = i + 1) begin : carry_gen
                assign c[i+1] = g[i] | (p[i] & c[i]);
            end
        endgenerate

    assign sum = p ^ c[3:0];
    assign Cout = c[4];

    // Групповые сигналы Propagate и Generate для всего блока
    assign GP = ~(&p);
    assign GG = ~(g[3] | (p[3] & g[2]) | (p[3] & p[2] & g[1]) | (p[3] & p[2] & p[1] & g[0]));
endmodule
*/

/* Code of fulladd4:
module fulladd4(
    input Cin,
    input [3:0] a, b,
    output [3:0] sum,
    output Cout,
    output wire GP, GG
);
    wire [3:0] p, g;
    wire [4:0] c; // Изменено на [4:0] для включения Cin

    assign p = a ^ b;
    assign g = a & b;

    assign c[0] = Cin;
    genvar i;
        generate
            for (i = 0; i < 4; i = i + 1) begin : carry_gen
                assign c[i+1] = g[i] | (p[i] & c[i]);
            end
        endgenerate

    assign sum = p ^ c[3:0];
    assign Cout = c[4];

    // Групповые сигналы Propagate и Generate для всего блока
     assign GP = ~(&p);
    assign GG = ~(g[3] | (p[3] & g[2]) | (p[3] & p[2] & g[1]) | (p[3] & p[2] & p[1] & g[0]));
endmodule
*/

/* Code of cla_ic_74182b:
module cla_ic_74182b (
    input[3:0]  PB, 
    input[3:0]  GB,
    input   Cn,
    output	PBo, GBo, Cnx, Cny, Cnz
);
    assign PBo = (  PB[0] |   PB[1]   |   PB[2]   |   PB[3]);
    assign GBo = (  (GB[0]  &   GB[1]   &   GB[2]   &   GB[3]) | 
                    (PB[1]  &   GB[1]   &   GB[2]   &   GB[3]) | 
                    (PB[2]  &   GB[2]   &   GB[3]) | 
                    (PB[3]  &   GB[3]));

    assign Cnx = ~( (PB[0]  &   GB[0]) | 
                    (GB[0]  &   ~Cn));
    assign Cny = ~( (PB[1]  &   GB[1]) | 
                    (PB[0]  &   GB[0]   &   GB[1])  |
                    (GB[0]  &   GB[1]   &   ~Cn));
    assign Cnz = ~( (PB[2]  &   GB[2]) | 
                    (PB[1]  &   GB[1]   &   GB[2])  |
                    (PB[0]  &   GB[0]   &   GB[1]   &   GB[2])  | 
                    (GB[0]  &   GB[1]   &   GB[2]   &   ~Cn));
endmodule
*/
