// Digital circuit CLA_74882_model.dig as structural Verilog
module CLA_74882_model (
  input  [7:0] nP_0,
  input  [7:0] nG_4,
  input  Cn,
  input  [7:0] nG_3,
  input  [7:0] nG_2,
  input  [7:0] nG_1,
  input  [7:0] nG_0,
  input  [7:0] nG_7,
  input  [7:0] nG_6,
  input  [7:0] nG_5,
  input  [7:0] nP_1,
  input  [7:0] nP_2,
  input  [7:0] nP_3,
  input  [7:0] nP_4,
  input  [7:0] nP_5,
  input  [7:0] nP_6,
  input  [7:0] nP_7,
  output C_n32,
  output C_n24,
  output C_n16,
  output C_n8
);

  wire and_1_out, and_2_out, and_3_out, and_4_out, and_5_out, and_6_out, and_7_out, and_8_out, and_9_out,
       and_10_out, and_11_out, and_12_out, and_13_out, and_14_out, and_15_out, and_16_out, and_17_out,
       and_18_out, and_19_out, and_20_out, and_21_out, and_22_out, and_23_out, and_24_out, not_1_out;

  not not_1 (not_1_out, Cn);
  and and_1 (and_1_out, nG_7[0], nP_7[0]);
  and and_2 (and_2_out, nG_7[0], nG_6[0], nP_6[0]);
  and and_3 (and_3_out, nG_7[0], nG_6[0], nG_5[0], nP_5[0]);
  and and_4 (and_4_out, nG_7[0], nG_6[0], nG_5[0], nG_4[0], nP_4[0]);
  and and_5 (and_5_out, nG_7[0], nG_6[0], nG_5[0], nG_4[0], nG_3[0], nP_3[0]);
  and and_6 (and_6_out, nG_7[0], nG_6[0], nG_5[0], nG_4[0], nG_3[0], nG_2[0], nP_2[0]);
  and and_7 (and_7_out, nG_7[0], nG_6[0], nG_5[0], nG_4[0], nG_3[0], nG_2[0], nG_1[0], nP_1[0]);
  and and_8 (and_8_out, nG_7[0], nG_6[0], nG_5[0], nG_4[0], nG_3[0], nG_2[0], nG_1[0], nG_0[0], nP_0[0]);
  and and_9 (and_9_out, nG_7[0], nG_6[0], nG_5[0], nG_4[0], nG_3[0], nG_2[0], nG_1[0], nG_0[0], not_1_out);
  and and_10 (and_10_out, nG_5[0], nP_5[0]);
  and and_11 (and_11_out, nG_5[0], nG_4[0], nP_4[0]);
  and and_12 (and_12_out, nG_5[0], nG_4[0], nG_3[0], nG_2[0], nP_3[0]);
  and and_13 (and_13_out, nG_5[0], nG_4[0], nG_3[0], nG_2[0], nP_2[0]);
  and and_14 (and_14_out, nG_5[0], nG_4[0], nG_3[0], nG_2[0], nG_1[0], nP_1[0]);
  and and_15 (and_15_out, nG_5[0], nG_4[0], nG_3[0], nG_2[0], nG_1[0], nG_0[0], nP_0[0]);
  and and_16 (and_16_out, nG_5[0], nG_4[0], nG_3[0], nG_2[0], nG_1[0], nG_0[0], not_1_out);
  and and_17 (and_17_out, nG_3[0], nP_3[0]);
  and and_18 (and_18_out, nG_3[0], nG_2[0], nP_2[0]);
  and and_19 (and_19_out, nG_3[0], nG_2[0], nG_1[0], nP_1[0]);
  and and_20 (and_20_out, nG_3[0], nG_2[0], nG_1[0], nG_0[0], nP_0[0]);
  and and_21 (and_21_out, nG_3[0], nG_2[0], nG_1[0], nG_0[0], not_1_out);
  and and_22 (and_22_out, nG_1[0], nP_1[0]);
  and and_23 (and_23_out, nG_1[0], nG_0[0], nP_0[0]);
  and and_24 (and_24_out, nG_1[0], nG_0[0], not_1_out);
  nor nor_1 (C_n24, and_10_out, and_11_out, and_12_out, and_13_out, and_14_out, and_15_out, and_16_out);
  nor nor_2 (C_n16, and_17_out, and_18_out, and_19_out, and_20_out, and_21_out);
  nor nor_3 (C_n8, and_22_out, and_23_out, and_24_out);
  nor nor_4 (C_n32, and_1_out, and_2_out, and_3_out, and_4_out, and_5_out, and_6_out, and_7_out, and_8_out, and_9_out);
  // Pins of 1 and 8 bits meet at nG_7
  // Pins of 1 and 8 bits meet at nP_7
  // Pins of 1 and 8 bits meet at nG_6
  // Pins of 1 and 8 bits meet at nP_6
  // Pins of 1 and 8 bits meet at nG_5
  // Pins of 1 and 8 bits meet at nP_5
  // Pins of 1 and 8 bits meet at nG_4
  // Pins of 1 and 8 bits meet at nP_4
  // Pins of 1 and 8 bits meet at nG_1
  // Pins of 1 and 8 bits meet at nP_1
  // Pins of 1 and 8 bits meet at nG_0
  // Pins of 1 and 8 bits meet at nP_0
endmodule
