// Digital circuit CLA_ADDER_4b.dig as structural Verilog
module CLA_ADDER_4b (
  input  [3:0] B__3_0,
  input  [3:0] A__3_0,
  input  C_in,
  output GP,
  output [3:0] Summ__3_0,
  output GG,
  output Cout
);

  fulladd4 #(.applicationType("IVERILOG")) u_fulladd4 (
    .a(A__3_0), .b(B__3_0), .Cin(C_in), .sum(Summ__3_0), .Cout(Cout), .GP(GP), .GG(GG));
endmodule

/* Code of fulladd4:
module fulladd4(
    input Cin,
    input [3:0] a, b,
    output [3:0] sum,
    output Cout,
    output wire GP, GG
);
    wire [3:0] p, g;
    wire [4:0] c; // Изменено на [4:0] для включения Cin

    assign p = a ^ b;
    assign g = a & b;

    assign c[0] = Cin;
    genvar i;
        generate
            for (i = 0; i < 4; i = i + 1) begin : carry_gen
                assign c[i+1] = g[i] | (p[i] & c[i]);
            end
        endgenerate

    assign sum = p ^ c[3:0];
    assign Cout = c[4];

    // Групповые сигналы Propagate и Generate для всего блока
    assign GP = &p;
    assign GG = g[3] | (p[3] & g[2]) | (p[3] & p[2] & g[1]) | (p[3] & p[2] & p[1] & g[0]);

endmodule
*/
