// Digital circuit CLA_adder32.dig as structural Verilog
module CLA_adder32 (
  input  C_in,
  input  [31:0] A__31_0,
  input  [31:0] B_31_0,
  output [3:0] Sum__3_0,
  output [3:0] Sum__7_4,
  output [3:0] Sum__11_8,
  output [3:0] Sum__15_12,
  output [32:0] Sum__32_0,
  output [3:0] Sum__19_16,
  output [3:0] Sum__23_20,
  output [3:0] Sum__27_24,
  output [3:0] Sum__31_28,
  output C_out
);

  wire _74882_1_p6, _74882_1_p11, _74882_1_p19, u_fulladd4_2_ngg, u_fulladd4_2_ngp, u_fulladd4_3_cout,
       u_fulladd4_3_ngg, u_fulladd4_3_ngp, u_fulladd4_4_ngg, u_fulladd4_4_ngp, u_fulladd4_5_cout,
       u_fulladd4_5_ngg, u_fulladd4_5_ngp, u_fulladd4_6_ngg, u_fulladd4_6_ngp, u_fulladd4_7_cout,
       u_fulladd4_7_ngg, u_fulladd4_7_ngp, u_fulladd4_8_ngg, u_fulladd4_8_ngp, u_fulladd4_cout,
       u_fulladd4_ngg, u_fulladd4_ngp;

  fulladd4 #(.applicationType("IVERILOG")) u_fulladd4 (
    .Cin(C_in), .a(A__31_0[3:0]), .b(B_31_0[3:0]), .sum(Sum__3_0), .Cout(u_fulladd4_cout),
    .nGP(u_fulladd4_ngp), .nGG(u_fulladd4_ngg));
  fulladd4 #(.applicationType("IVERILOG")) u_fulladd4_2 (
    .Cin(u_fulladd4_cout), .a(A__31_0[7:4]), .b(B_31_0[7:4]), .sum(Sum__7_4), .nGP(u_fulladd4_2_ngp),
    .nGG(u_fulladd4_2_ngg));  // open: Cout
  fulladd4 #(.applicationType("IVERILOG")) u_fulladd4_3 (
    .Cin(_74882_1_p6), .a(A__31_0[11:8]), .b(B_31_0[11:8]), .sum(Sum__11_8), .Cout(u_fulladd4_3_cout),
    .nGP(u_fulladd4_3_ngp), .nGG(u_fulladd4_3_ngg));
  fulladd4 #(.applicationType("IVERILOG")) u_fulladd4_4 (
    .Cin(u_fulladd4_3_cout), .a(A__31_0[15:12]), .b(B_31_0[15:12]), .sum(Sum__15_12), .nGP(u_fulladd4_4_ngp),
    .nGG(u_fulladd4_4_ngg));  // open: Cout
  fulladd4 #(.applicationType("IVERILOG")) u_fulladd4_5 (
    .Cin(_74882_1_p11), .a(A__31_0[19:16]), .b(B_31_0[19:16]), .sum(Sum__19_16), .Cout(u_fulladd4_5_cout),
    .nGP(u_fulladd4_5_ngp), .nGG(u_fulladd4_5_ngg));
  fulladd4 #(.applicationType("IVERILOG")) u_fulladd4_6 (
    .Cin(u_fulladd4_5_cout), .a(A__31_0[23:20]), .b(B_31_0[23:20]), .sum(Sum__23_20), .nGP(u_fulladd4_6_ngp),
    .nGG(u_fulladd4_6_ngg));  // open: Cout
  fulladd4 #(.applicationType("IVERILOG")) u_fulladd4_7 (
    .Cin(_74882_1_p19), .a(A__31_0[27:24]), .b(B_31_0[27:24]), .sum(Sum__27_24), .Cout(u_fulladd4_7_cout),
    .nGP(u_fulladd4_7_ngp), .nGG(u_fulladd4_7_ngg));
  fulladd4 #(.applicationType("IVERILOG")) u_fulladd4_8 (
    .Cin(u_fulladd4_7_cout), .a(A__31_0[31:28]), .b(B_31_0[31:28]), .sum(Sum__31_28), .nGP(u_fulladd4_8_ngp),
    .nGG(u_fulladd4_8_ngg));  // open: Cout
  // _74882 _74882_1: pin names not known; wires that end beside it: C_in, u_fulladd4_ngg, u_fulladd4_ngp, u_fulladd4_2_ngg, u_fulladd4_2_ngp, _74882_1_p6, u_fulladd4_3_ngg, u_fulladd4_3_ngp, u_fulladd4_4_ngg, u_fulladd4_4_ngp, _74882_1_p11, 1'b0, 1'b1, C_out, u_fulladd4_8_ngp, u_fulladd4_8_ngg, u_fulladd4_7_ngp, u_fulladd4_7_ngg, _74882_1_p19, u_fulladd4_6_ngp, u_fulladd4_6_ngg, u_fulladd4_5_ngp, u_fulladd4_5_ngg

  assign Sum__32_0 = {C_out, Sum__31_28, Sum__27_24, Sum__23_20, Sum__19_16, Sum__15_12, Sum__11_8, Sum__7_4, Sum__3_0};
endmodule

/* Code of fulladd4:
module fulladd4(
    input Cin,
    input [3:0] a, b,
    output [3:0] sum,
    output Cout,
    output wire nGP, nGG
);
    wire [3:0] p, g;
    wire [4:0] c; // Изменено на [4:0] для включения Cin

    assign p = a ^ b;
    assign g = a & b;

    assign c[0] = Cin;
    genvar i;
        generate
            for (i = 0; i < 4; i = i + 1) begin : carry_gen
                assign c[i+1] = g[i] | (p[i] & c[i]);
            end
        endgenerate

    assign sum = p ^ c[3:0];
    assign Cout = c[4];

    // Групповые сигналы Propagate и Generate для всего блока
    assign nGP = ~(&p);
    assign nGG = ~(g[3] | (p[3] & g[2]) | (p[3] & p[2] & g[1]) | (p[3] & p[2] & p[1] & g[0]));

endmodule
*/
