// Digital circuit CLA_adder_74882.dig as structural Verilog
module CLA_adder_74882 (
  input  C_in,
  input  [31:0] A__31_0,
  input  [31:0] B__31_0,
  output [3:0] Sum__3_0,
  output [3:0] Sum__4_7,
  output [3:0] Sum__11_8,
  output [3:0] Sum__15_12,
  output [32:0] Summ_32_0,
  output [3:0] Sum__19_16,
  output [3:0] Sum__23_20,
  output [3:0] Sum__27_23,
  output [3:0] Sum__31_28,
  output C_out
);

  wire u_fulladd4_3_cout, u_fulladd4_5_cout, u_fulladd4_7_cout, u_fulladd4_cout;
  wire [2:0] u_carry32_n74882_cout;
  wire [7:0] u_fulladd4_ngg, u_fulladd4_ngp;

  fulladd4 #(.applicationType("IVERILOG")) u_fulladd4 (
    .Cin(C_in), .a(A__31_0[3:0]), .b(B__31_0[3:0]), .sum(Sum__3_0), .Cout(u_fulladd4_cout),
    .nGP(u_fulladd4_ngp[0]), .nGG(u_fulladd4_ngg[0]));
  fulladd4 #(.applicationType("IVERILOG")) u_fulladd4_2 (
    .Cin(u_fulladd4_cout), .a(A__31_0[7:4]), .b(B__31_0[7:4]), .sum(Sum__4_7), .nGP(u_fulladd4_ngp[1]),
    .nGG(u_fulladd4_ngg[1]));  // open: Cout
  fulladd4 #(.applicationType("IVERILOG")) u_fulladd4_3 (
    .Cin(u_carry32_n74882_cout[0]), .a(A__31_0[11:8]), .b(B__31_0[11:8]), .sum(Sum__11_8),
    .Cout(u_fulladd4_3_cout), .nGP(u_fulladd4_ngp[2]), .nGG(u_fulladd4_ngg[2]));
  fulladd4 #(.applicationType("IVERILOG")) u_fulladd4_4 (
    .Cin(u_fulladd4_3_cout), .a(A__31_0[15:12]), .b(B__31_0[15:12]), .sum(Sum__15_12),
    .nGP(u_fulladd4_ngp[3]), .nGG(u_fulladd4_ngg[3]));  // open: Cout
  fulladd4 #(.applicationType("IVERILOG")) u_fulladd4_5 (
    .Cin(u_carry32_n74882_cout[1]), .a(A__31_0[19:16]), .b(B__31_0[19:16]), .sum(Sum__19_16),
    .Cout(u_fulladd4_5_cout), .nGP(u_fulladd4_ngp[4]), .nGG(u_fulladd4_ngg[4]));
  fulladd4 #(.applicationType("IVERILOG")) u_fulladd4_6 (
    .Cin(u_fulladd4_5_cout), .a(A__31_0[23:20]), .b(B__31_0[23:20]), .sum(Sum__23_20),
    .nGP(u_fulladd4_ngp[5]), .nGG(u_fulladd4_ngg[5]));  // open: Cout
  fulladd4 #(.applicationType("IVERILOG")) u_fulladd4_7 (
    .Cin(u_carry32_n74882_cout[2]), .a(A__31_0[27:24]), .b(B__31_0[27:24]), .sum(Sum__27_23),
    .Cout(u_fulladd4_7_cout), .nGP(u_fulladd4_ngp[6]), .nGG(u_fulladd4_ngg[6]));
  fulladd4 #(.applicationType("IVERILOG")) u_fulladd4_8 (
    .Cin(u_fulladd4_7_cout), .a(A__31_0[31:28]), .b(B__31_0[31:28]), .sum(Sum__31_28),
    .nGP(u_fulladd4_ngp[7]), .nGG(u_fulladd4_ngg[7]));  // open: Cout
  carry32_n74882 #(.applicationType("IVERILOG")) u_carry32_n74882 (
    .Cin(C_in), .P(u_fulladd4_ngp), .G(u_fulladd4_ngg), .Cout({C_out, u_carry32_n74882_cout}));

  assign Summ_32_0 = {C_out, Sum__31_28, Sum__27_23, Sum__23_20, Sum__19_16, Sum__15_12, Sum__11_8, Sum__4_7, Sum__3_0};
endmodule

/* Code of fulladd4:
module fulladd4(
    input Cin,
    input [3:0] a, b,
    output [3:0] sum,
    output Cout,
    output wire nGP, nGG
);
    wire [3:0] p, g;
    wire [4:0] c; // Изменено на [4:0] для включения Cin

    assign p = a ^ b;
    assign g = a & b;

    assign c[0] = Cin;
    genvar i;
        generate
            for (i = 0; i < 4; i = i + 1) begin : carry_gen
                assign c[i+1] = g[i] | (p[i] & c[i]);
            end
        endgenerate

    assign sum = p ^ c[3:0];
    assign Cout = c[4];

    // Групповые сигналы Propagate и Generate для всего блока
    assign nGP =~(&p);
    assign nGG =~(  (g[3]) | 
                    (p[3] & g[2]) |
                    (p[3] & p[2] & g[1]) |
                    (p[3] & p[2] & p[1] & g[0]));

endmodule
*/

/* Code of fulladd4:
module fulladd4(
    input Cin,
    input [3:0] a, b,
    output [3:0] sum,
    output Cout,
    output wire nGP, nGG
);
    wire [3:0] p, g;
    wire [4:0] c; // Изменено на [4:0] для включения Cin

    assign p = a ^ b;
    assign g = a & b;

    assign c[0] = Cin;
    genvar i;
        generate
            for (i = 0; i < 4; i = i + 1) begin : carry_gen
                assign c[i+1] = g[i] | (p[i] & c[i]);
            end
        endgenerate

    assign sum = p ^ c[3:0];
    assign Cout = c[4];

    // Групповые сигналы Propagate и Generate для всего блока
    assign nGP =~(&p);
    assign nGG =~(
	(g[3]) | 
	(p[3] & g[2]) |
	(p[3] & p[2] & g[1]) |
	(p[3] & p[2] & p[1] & g[0]));

endmodule
*/

/* Code of carry32_n74882:
module carry32_n74882 (
    input [7:0] P,      // Пропускные сигналы
    input [7:0] G,      // Генерирующие сигналы
    input Cin,          // Входной перенос
    output [3:0] Cout   // Выходные переносы
);


    // Активный уровень - 0
    assign Cout[0] = ~((G[1]) & P[1]  | 
                    (&(G[1:0]) & P[0] )| 
                    (&(G[1:0]) & ~Cin));

    assign Cout[1] = ~  ((G[3] & P[3]) | 
                        (&(G[3:2]) & P[2]) |
                        (&(G[3:1]) & P[1]) |
                        (&(G[3:0]) & P[0]) |
                        (&(G[3:0]) & ~Cin));

    // Активный уровень - 0
    assign Cout[2] = ~((G[5] & P[5]) |
                       (&(G[5:4]) & P[4]) |
                       (&(G[5:3]) & P[3]) |
                       (&(G[5:2]) & P[2]) |
                       (&(G[5:1]) & P[1]) |
                       (&(G[5:0]) & P[0]) |
                       (&(G[5:0]) & ~Cin));

    assign Cout[3] = ~((G[7] & P[7]) |
                       (&(G[7:6]) & P[6]) |
                       (&(G[7:5]) & P[5]) |
                       (&(G[7:4]) & P[4]) |
                       (&(G[7:3]) & P[3]) |
                       (&(G[7:2]) & P[2]) |
                       (&(G[7:1]) & P[1]) |
                       (&(G[7:0]) & P[0]) |
                       (&(G[7:0]) & ~Cin));

endmodule
*/
