// Digital circuit mod_74882.dig as structural Verilog
module mod_74882 (
  input  [7:0] nP,
  input  [7:0] nG,
  input  Cn,
  input  nLow_High,
  input  [3:0] A,
  input  [3:0] B,
  input  CnA,
  input  [3:0] A_2,
  input  [3:0] B_2,
  input  CnA_2,
  input  [2:0] Cmd,
  input  C_in,
  input  [31:0] A_3,
  input  [31:0] B_3,
  output C_n32,
  output C_n24,
  output C_n16,
  output C_n8,
  output [3:0] out_12,
  output [3:0] out_17,
  output [3:0] Sum_4,
  output [3:0] Sum_5,
  output [3:0] Sum_6,
  output [3:0] Sum_7,
  output [31:0] SumS_total,
  output [3:0] Sum_8,
  output [3:0] Sum_9,
  output [3:0] Sum_10,
  output [3:0] Sum_11
);

  wire _74182_1_pin9, _74182_1_pin11, _74182_1_pin12, _74381_1_pin13, _74381_1_pin14, and_1_out, and_2_out,
       and_3_out, and_4_out, and_5_out, and_6_out, and_7_out, and_8_out, and_9_out, and_10_out, and_11_out,
       and_12_out, and_13_out, and_14_out, and_15_out, and_16_out, and_17_out, and_18_out, and_19_out,
       and_20_out, and_21_out, and_22_out, and_23_out, and_24_out, and_25_out, and_26_out, and_27_out,
       and_28_out, not_1_out, u_fulladd4_3_cout, u_fulladd4_5_cout, u_fulladd4_7_cout, u_fulladd4_cout,
       xor_1_out, xor_2_out, xor_3_out, xor_4_out;
  wire [3:0] u_CarryLookaheadUnit_74882_cout;
  wire [7:0] bitextender_1_out, u_fulladd4_ngg, u_fulladd4_ngp, xor_9_out, xor_10_out;

  xor xor_1 (xor_1_out, A[0], B[0]);
  and and_1 (and_1_out, A[0], B[0]);
  xor xor_2 (xor_2_out, A[1], B[1]);
  and and_2 (and_2_out, A[1], B[1]);
  xor xor_3 (xor_3_out, A[2], B[2]);
  and and_3 (and_3_out, A[2], B[2]);
  xor xor_4 (xor_4_out, A[3], B[3]);
  and and_4 (and_4_out, A[3], B[3]);
  _74182 _74182_1 (
    .pin1(and_2_out), .pin2(xor_2_out), .pin3(and_1_out), .pin4(xor_1_out), .pin5(and_4_out),
    .pin6(xor_4_out), .pin8(1'b0), .pin9(_74182_1_pin9), .pin11(_74182_1_pin11), .pin12(_74182_1_pin12),
    .pin13(CnA), .pin14(and_3_out), .pin15(xor_3_out), .pin16(1'b1));  // open: pin7, pin10
  _74381 _74381_1 (
    .pin1(A_2[1]), .pin2(B_2[0]), .pin3(A_2[0]), .pin4(B_2[1]), .pin5(Cmd[0]), .pin6(Cmd[1]), .pin7(Cmd[2]),
    .pin8(out_17[0]), .pin9(out_17[1]), .pin10(1'b0), .pin11(out_17[2]), .pin12(out_17[3]),
    .pin13(_74381_1_pin13), .pin14(_74381_1_pin14), .pin15(CnA_2), .pin16(B_2[3]), .pin17(A_2[3]),
    .pin18(B_2[2]), .pin19(A_2[2]), .pin20(1'b1));
  xor xor_5 (out_12[0], xor_1_out, CnA);
  xor xor_6 (out_12[1], xor_2_out, _74182_1_pin12);
  xor xor_7 (out_12[2], _74182_1_pin11, xor_3_out);
  xor xor_8 (out_12[3], xor_4_out, _74182_1_pin9);
  LED led_1 (.in(_74381_1_pin14));
  LED led_2 (.in(_74381_1_pin13));
  BitExtender #(.inputBits(1), .outputBits(8)) bitextender_1 (.in(nLow_High), .out(bitextender_1_out));
  assign xor_9_out = nG ^ bitextender_1_out;  // XOr xor_9, 8 bits wide
  assign xor_10_out = bitextender_1_out ^ nP;  // XOr xor_10, 8 bits wide
  not not_1 (not_1_out, Cn);
  and and_5 (and_5_out, xor_9_out[7], xor_10_out[7]);
  and and_6 (and_6_out, xor_9_out[7], xor_9_out[6], xor_10_out[6]);
  and and_7 (and_7_out, xor_9_out[7], xor_9_out[6], xor_9_out[5], xor_10_out[5]);
  and and_8 (and_8_out, xor_9_out[7], xor_9_out[6], xor_9_out[5], xor_9_out[4], xor_10_out[4]);
  and and_9 (and_9_out, xor_9_out[7], xor_9_out[6], xor_9_out[5], xor_9_out[4], xor_9_out[3], xor_10_out[3]);
  and and_10 (and_10_out, xor_9_out[7], xor_9_out[6], xor_9_out[5], xor_9_out[4], xor_9_out[3], xor_9_out[2], xor_10_out[2]);
  and and_11 (and_11_out, xor_9_out[7], xor_9_out[6], xor_9_out[5], xor_9_out[4], xor_9_out[3], xor_9_out[2], xor_9_out[1], xor_10_out[1]);
  and and_12 (and_12_out, xor_9_out[7], xor_9_out[6], xor_9_out[5], xor_9_out[4], xor_9_out[3], xor_9_out[2], xor_9_out[1], xor_9_out[0], xor_10_out[0]);
  and and_13 (and_13_out, xor_9_out[7], xor_9_out[6], xor_9_out[5], xor_9_out[4], xor_9_out[3], xor_9_out[2], xor_9_out[1], xor_9_out[0], not_1_out);
  and and_14 (and_14_out, xor_9_out[5], xor_10_out[5]);
  and and_15 (and_15_out, xor_9_out[5], xor_9_out[4], xor_10_out[4]);
  and and_16 (and_16_out, xor_9_out[5], xor_9_out[4], xor_9_out[3], xor_9_out[2], xor_10_out[3]);
  and and_17 (and_17_out, xor_9_out[5], xor_9_out[4], xor_9_out[3], xor_9_out[2], xor_10_out[2]);
  and and_18 (and_18_out, xor_9_out[5], xor_9_out[4], xor_9_out[3], xor_9_out[2], xor_9_out[1], xor_10_out[1]);
  and and_19 (and_19_out, xor_9_out[5], xor_9_out[4], xor_9_out[3], xor_9_out[2], xor_9_out[1], xor_9_out[0], xor_10_out[0]);
  and and_20 (and_20_out, xor_9_out[5], xor_9_out[4], xor_9_out[3], xor_9_out[2], xor_9_out[1], xor_9_out[0], not_1_out);
  and and_21 (and_21_out, xor_9_out[3], xor_10_out[3]);
  and and_22 (and_22_out, xor_9_out[3], xor_9_out[2], xor_10_out[2]);
  and and_23 (and_23_out, xor_9_out[3], xor_9_out[2], xor_9_out[1], xor_10_out[1]);
  and and_24 (and_24_out, xor_9_out[3], xor_9_out[2], xor_9_out[1], xor_9_out[0], xor_10_out[0]);
  and and_25 (and_25_out, xor_9_out[3], xor_9_out[2], xor_9_out[1], xor_9_out[0], not_1_out);
  and and_26 (and_26_out, xor_9_out[1], xor_10_out[1]);
  and and_27 (and_27_out, xor_9_out[1], xor_9_out[0], xor_10_out[0]);
  and and_28 (and_28_out, xor_9_out[1], xor_9_out[0], not_1_out);
  nor nor_1 (C_n24, and_14_out, and_15_out, and_16_out, and_17_out, and_18_out, and_19_out, and_20_out);
  nor nor_2 (C_n16, and_21_out, and_22_out, and_23_out, and_24_out, and_25_out);
  nor nor_3 (C_n8, and_26_out, and_27_out, and_28_out);
  nor nor_4 (C_n32, and_5_out, and_6_out, and_7_out, and_8_out, and_9_out, and_10_out, and_11_out, and_12_out, and_13_out);
  fulladd4 #(.applicationType("IVERILOG")) u_fulladd4 (
    .Cin(C_in), .a(A_3[3:0]), .b(B_3[3:0]), .sum(Sum_4), .Cout(u_fulladd4_cout), .nGP(u_fulladd4_ngp[0]),
    .nGG(u_fulladd4_ngg[0]));
  fulladd4 #(.applicationType("IVERILOG")) u_fulladd4_2 (
    .Cin(u_fulladd4_cout), .a(A_3[7:4]), .b(B_3[7:4]), .sum(Sum_5), .nGP(u_fulladd4_ngp[1]),
    .nGG(u_fulladd4_ngg[1]));  // open: Cout
  fulladd4 #(.applicationType("IVERILOG")) u_fulladd4_3 (
    .Cin(u_CarryLookaheadUnit_74882_cout[0]), .a(A_3[11:8]), .b(B_3[11:8]), .sum(Sum_6),
    .Cout(u_fulladd4_3_cout), .nGP(u_fulladd4_ngp[2]), .nGG(u_fulladd4_ngg[2]));
  fulladd4 #(.applicationType("IVERILOG")) u_fulladd4_4 (
    .Cin(u_fulladd4_3_cout), .a(A_3[15:12]), .b(B_3[15:12]), .sum(Sum_7), .nGP(u_fulladd4_ngp[3]),
    .nGG(u_fulladd4_ngg[3]));  // open: Cout
  fulladd4 #(.applicationType("IVERILOG")) u_fulladd4_5 (
    .Cin(u_CarryLookaheadUnit_74882_cout[1]), .a(A_3[19:16]), .b(B_3[19:16]), .sum(Sum_8),
    .Cout(u_fulladd4_5_cout), .nGP(u_fulladd4_ngp[4]), .nGG(u_fulladd4_ngg[4]));
  fulladd4 #(.applicationType("IVERILOG")) u_fulladd4_6 (
    .Cin(u_fulladd4_5_cout), .a(A_3[23:20]), .b(B_3[23:20]), .sum(Sum_9), .nGP(u_fulladd4_ngp[5]),
    .nGG(u_fulladd4_ngg[5]));  // open: Cout
  fulladd4 #(.applicationType("IVERILOG")) u_fulladd4_7 (
    .Cin(u_CarryLookaheadUnit_74882_cout[2]), .a(A_3[27:24]), .b(B_3[27:24]), .sum(Sum_10),
    .Cout(u_fulladd4_7_cout), .nGP(u_fulladd4_ngp[6]), .nGG(u_fulladd4_ngg[6]));
  fulladd4 #(.applicationType("IVERILOG")) u_fulladd4_8 (
    .Cin(u_fulladd4_7_cout), .a(A_3[31:28]), .b(B_3[31:28]), .sum(Sum_11), .nGP(u_fulladd4_ngp[7]),
    .nGG(u_fulladd4_ngg[7]));  // open: Cout
  CarryLookaheadUnit_74882 #(.applicationType("IVERILOG")) u_CarryLookaheadUnit_74882 (
    .P(u_fulladd4_ngp), .G(u_fulladd4_ngg), .Cin(C_in), .Cout(u_CarryLookaheadUnit_74882_cout));

  assign SumS_total = {Sum_11, Sum_10, Sum_9, Sum_8, Sum_7, Sum_6, Sum_5, Sum_4};
endmodule

/* Code of fulladd4:
module fulladd4(
    input Cin,
    input [3:0] a, b,
    output [3:0] sum,
    output Cout,
    output wire nGP, nGG
);
    wire [3:0] p, g;
    wire [4:0] c; // Изменено на [4:0] для включения Cin

    assign p = a ^ b;
    assign g = a & b;

    assign c[0] = Cin;
    genvar i;
        generate
            for (i = 0; i < 4; i = i + 1) begin : carry_gen
                assign c[i+1] = g[i] | (p[i] & c[i]);
            end
        endgenerate

    assign sum = p ^ c[3:0];
    assign Cout = c[4];

    // Групповые сигналы Propagate и Generate для всего блока
    assign nGP = ~(&p);
    assign nGG = ~(g[3] | (p[3] & g[2]) | (p[3] & p[2] & g[1]) | (p[3] & p[2] & p[1] & g[0]));

endmodule
*/

/* Code of CarryLookaheadUnit_74882:
module CarryLookaheadUnit_74882 (
    input [7:0] P,  // Пропускные сигналы
    input [7:0] G,  // Генерирующие сигналы
    input Cin,      // Входной перенос
    output [3:0] Cout  // Выходные переносы
);

    // Сокращенные записи с использованием generate
    genvar i;
    wire [7:0] PP;  // PP[i] = P[i] & P[i-1]
    wire [7:0] PG;  // PG[i] = P[i] & G[i-1]

    generate
        for (i = 1; i <= 7; i = i + 1) begin : gen_PP_PG
            assign PP[i] = P[i] & P[i-1];
            assign PG[i] = P[i] & G[i-1];
        end
    endgenerate

    // Вычисление Cout
    assign Cout[0] = G[0] | P[0] & Cin;
    assign Cout[1] = G[1] | P[1] & G[0] | P[1] & P[0] & Cin;
    assign Cout[2] = G[2] | P[2] & G[1] | P[2] & P[1] & G[0] | P[2] & P[1] & P[0] & Cin;
    assign Cout[3] = G[3] | P[3] & G[2] | P[3] & P[2] & G[1] | P[3] & P[2] & P[1] & G[0] | P[3] & P[2] & P[1] & P[0] & Cin;

endmodule
*/
