// Digital circuit 74381_cascade.dig as structural Verilog
module _74381_cascade (
  input  [15:0] A,
  input  [15:0] B,
  input  CnA,
  input  [2:0] Cmd,
  output [3:0] out_5,
  output [3:0] Res__11_8,
  output [3:0] Res__15_12,
  output [16:0] Out,
  output [3:0] Res__7_3,
  output Out_2
);

  wire _74381_1_pin13, _74381_1_pin14, _74381_2_pin13, _74381_2_pin14, _74381_2_pin15, _74381_3_pin13,
       _74381_3_pin14, _74381_3_pin15, _74382_1_pin15;

  _74381 _74381_1 (
    .pin1(A[1]), .pin2(B[1]), .pin3(A[0]), .pin4(B[0]), .pin5(Cmd[0]), .pin6(Cmd[1]), .pin7(Cmd[2]),
    .pin8(Out[0]), .pin9(Out[1]), .pin10(1'b0), .pin11(Out[2]), .pin12(Out[3]), .pin13(_74381_1_pin13),
    .pin14(_74381_1_pin14), .pin15(CnA), .pin16(B[3]), .pin17(A[3]), .pin18(B[2]), .pin19(A[2]), .pin20(1'b1));
  _74381 _74381_2 (
    .pin1(A[5]), .pin2(B[5]), .pin3(A[4]), .pin4(B[4]), .pin5(Cmd[0]), .pin6(Cmd[1]), .pin7(Cmd[2]),
    .pin8(Out[4]), .pin9(Out[5]), .pin10(1'b0), .pin11(Out[6]), .pin12(Out[7]), .pin13(_74381_2_pin13),
    .pin14(_74381_2_pin14), .pin15(_74381_2_pin15), .pin16(B[7]), .pin17(A[7]), .pin18(B[6]), .pin19(A[6]),
    .pin20(1'b1));
  _74381 _74381_3 (
    .pin1(A[9]), .pin2(B[9]), .pin3(A[8]), .pin4(B[8]), .pin5(Cmd[0]), .pin6(Cmd[1]), .pin7(Cmd[2]),
    .pin8(Out[8]), .pin9(Out[9]), .pin10(1'b0), .pin11(Out[10]), .pin12(Out[11]), .pin13(_74381_3_pin13),
    .pin14(_74381_3_pin14), .pin15(_74381_3_pin15), .pin16(B[11]), .pin17(A[11]), .pin18(B[10]),
    .pin19(A[10]), .pin20(1'b1));
  _74382 _74382_1 (
    .pin1(A[13]), .pin2(B[13]), .pin3(A[12]), .pin4(B[12]), .pin5(Cmd[0]), .pin6(Cmd[1]), .pin7(Cmd[2]),
    .pin8(Out[12]), .pin9(Out[13]), .pin10(1'b0), .pin11(Out[14]), .pin12(Out[15]), .pin13(Out_2),
    .pin14(Out[16]), .pin15(_74382_1_pin15), .pin16(B[15]), .pin17(A[15]), .pin18(B[14]), .pin19(A[14]),
    .pin20(1'b1));
  _74182 _74182_1 (
    .pin1(_74381_2_pin14), .pin2(_74381_2_pin13), .pin3(_74381_1_pin14), .pin4(_74381_1_pin13), .pin5(1'b1),
    .pin6(1'b1), .pin8(1'b0), .pin9(_74382_1_pin15), .pin11(_74381_3_pin15), .pin12(_74381_2_pin15),
    .pin13(CnA), .pin14(_74381_3_pin14), .pin15(_74381_3_pin13), .pin16(1'b1));  // open: pin7, pin10

  assign out_5 = Out[3:0];
  assign Res__7_3 = Out[7:4];
  assign Res__11_8 = Out[11:8];
  assign Res__15_12 = Out[15:12];

  // Other names for the same wires on the sheet: S_0 = Cmd[0]; S_1 = Cmd[1]; S_2 = Cmd[2]
endmodule
