// Digital circuit 74381_single.dig as structural Verilog
module _74381_single (
  input  [3:0] A,
  input  [3:0] B,
  input  CnA,
  input  [2:0] Cmd,
  output [3:0] out_5
);

  wire _74381_1_pin13, _74381_1_pin14;

  _74381 _74381_1 (
    .pin1(A[1]), .pin2(B[1]), .pin3(A[0]), .pin4(B[0]), .pin5(Cmd[0]), .pin6(Cmd[1]), .pin7(Cmd[2]),
    .pin8(out_5[0]), .pin9(out_5[1]), .pin10(1'b0), .pin11(out_5[2]), .pin12(out_5[3]),
    .pin13(_74381_1_pin13), .pin14(_74381_1_pin14), .pin15(CnA), .pin16(B[3]), .pin17(A[3]), .pin18(B[2]),
    .pin19(A[2]), .pin20(1'b1));
  LED led_1 (.in(_74381_1_pin14));
  LED led_2 (.in(_74381_1_pin13));

  // Other names for the same wires on the sheet: CMD_0 = Cmd[0]; CMD_1 = Cmd[1]; CMD_2 = Cmd[2]
endmodule
