// Digital circuit 74381_verilog.dig as structural Verilog
module _74381_verilog (
  input  [3:0] A,
  input  [3:0] B,
  input  C_in,
  input  [2:0] Cmd,
  input  [15:0] A_2,
  input  [15:0] B_2,
  input  CnA,
  input  [2:0] Cmd_2,
  output [3:0] RES
);

  wire u_alu_74381_5_ngg, u_alu_74381_5_ngp, u_cla_ic_74182b_cnx, u_cla_ic_74182b_cny, u_cla_ic_74182b_cnz;
  wire [3:0] u_alu_74381_ngg, u_alu_74381_ngp;

  alu_74381 #(.applicationType("IVERILOG")) u_alu_74381 (
    .A(A_2[3:0]), .B(B_2[3:0]), .S(Cmd_2), .Cin(CnA), .nGP(u_alu_74381_ngp[0]), .nGG(u_alu_74381_ngg[0]));  // open: F
  alu_74381 #(.applicationType("IVERILOG")) u_alu_74381_2 (
    .A(A_2[7:4]), .B(B_2[7:4]), .S(Cmd_2), .Cin(u_cla_ic_74182b_cnx), .nGP(u_alu_74381_ngp[1]),
    .nGG(u_alu_74381_ngg[1]));  // open: F
  alu_74381 #(.applicationType("IVERILOG")) u_alu_74381_3 (
    .A(A_2[11:8]), .B(B_2[11:8]), .S(Cmd_2), .Cin(u_cla_ic_74182b_cny), .nGP(u_alu_74381_ngp[2]),
    .nGG(u_alu_74381_ngg[2]));  // open: F
  alu_74381 #(.applicationType("IVERILOG")) u_alu_74381_4 (
    .A(A_2[15:12]), .B(B_2[15:12]), .S(Cmd_2), .Cin(u_cla_ic_74182b_cnz), .nGP(u_alu_74381_ngp[3]),
    .nGG(u_alu_74381_ngg[3]));  // open: F
  alu_74381 #(.applicationType("IVERILOG")) u_alu_74381_5 (
    .A(A), .B(B), .S(Cmd), .Cin(C_in), .nGP(u_alu_74381_5_ngp), .nGG(u_alu_74381_5_ngg), .F(RES));
  LED led_1 (.in(u_alu_74381_5_ngp));
  LED led_2 (.in(u_alu_74381_5_ngg));
  cla_ic_74182b #(.applicationType("IVERILOG")) u_cla_ic_74182b (
    .Cn(CnA), .PB(u_alu_74381_ngp), .GB(u_alu_74381_ngg), .Cnx(u_cla_ic_74182b_cnx),
    .Cny(u_cla_ic_74182b_cny), .Cnz(u_cla_ic_74182b_cnz));  // open: PBo, GBo
endmodule

/* Code of alu_74381:
module alu_74381 (
    input [3:0] A, B,
    input [2:0] S,
    input Cin,
    output wire nGP, nGG,
    output reg [3:0] F
);

endmodule
*/

/* Code of cla_ic_74182b:
module cla_ic_74182b (
    input[3:0]  PB, 
    input[3:0]  GB,
    input   Cn,
    output	PBo, GBo, Cnx, Cny, Cnz
);
    assign PBo = (  PB[0]   |   PB[1]   |   PB[2]   |   PB[3]);
    assign GBo = (  (GB[0]  &   GB[1]   &   GB[2]   &   GB[3]) | 
                    (PB[1]  &   GB[1]   &   GB[2]   &   GB[3]) | 
                    (PB[2]  &   GB[2]   &   GB[3]) | 
                    (PB[3]  &   GB[3]));

    assign Cnx = ~( (PB[0]  &   GB[0]) | 
                    (GB[0]  &   ~Cn));
    assign Cny = ~( (PB[1]  &   GB[1]) | 
                    (PB[0]  &   GB[0]   &   GB[1])  |
                    (GB[0]  &   GB[1]   &   ~Cn));
    assign Cnz = ~( (PB[2]  &   GB[2]) | 
                    (PB[1]  &   GB[1]   &   GB[2])  |
                    (PB[0]  &   GB[0]   &   GB[1]   &   GB[2])  | 
                    (GB[0]  &   GB[1]   &   GB[2]   &   ~Cn));
endmodule
*/
