// Digital circuit 74382_cascade.dig as structural Verilog
module _74382_cascade (
  input  [15:0] A,
  input  [15:0] B,
  input  CnA,
  input  [2:0] Cmd,
  output [15:0] Out,
  output out_6,
  output out_7
);

  wire _74382_1_pin13, _74382_1_pin14, _74382_2_pin14, _74382_3_pin14;

  _74382 _74382_1 (
    .pin1(A[1]), .pin2(B[1]), .pin3(A[0]), .pin4(B[0]), .pin5(Cmd[0]), .pin6(Cmd[1]), .pin7(Cmd[2]),
    .pin8(Out[0]), .pin9(Out[1]), .pin10(1'b0), .pin11(Out[2]), .pin12(Out[3]), .pin13(_74382_1_pin13),
    .pin14(_74382_1_pin14), .pin15(CnA), .pin16(B[3]), .pin17(A[3]), .pin18(B[2]), .pin19(A[2]), .pin20(1'b1));
  _74382 _74382_2 (
    .pin1(A[5]), .pin2(B[5]), .pin3(A[4]), .pin4(B[4]), .pin5(Cmd[0]), .pin6(Cmd[1]), .pin7(Cmd[2]),
    .pin8(Out[4]), .pin9(Out[5]), .pin10(1'b0), .pin11(Out[6]), .pin12(Out[7]), .pin14(_74382_2_pin14),
    .pin15(_74382_1_pin14), .pin16(B[7]), .pin17(A[7]), .pin18(B[6]), .pin19(A[6]), .pin20(1'b1));  // open: pin13
  _74382 _74382_3 (
    .pin1(A[9]), .pin2(B[9]), .pin3(A[8]), .pin4(B[8]), .pin5(Cmd[0]), .pin6(Cmd[1]), .pin7(Cmd[2]),
    .pin8(Out[8]), .pin9(Out[9]), .pin10(1'b0), .pin11(Out[10]), .pin12(Out[11]), .pin14(_74382_3_pin14),
    .pin15(_74382_2_pin14), .pin16(B[11]), .pin17(A[11]), .pin18(B[10]), .pin19(A[10]), .pin20(1'b1));  // open: pin13
  _74382 _74382_4 (
    .pin1(A[13]), .pin2(B[13]), .pin3(A[12]), .pin4(B[12]), .pin5(Cmd[0]), .pin6(Cmd[1]), .pin7(Cmd[2]),
    .pin8(Out[12]), .pin9(Out[13]), .pin10(1'b0), .pin11(Out[14]), .pin12(Out[15]), .pin13(out_7),
    .pin14(out_6), .pin15(_74382_3_pin14), .pin16(B[15]), .pin17(A[15]), .pin18(B[14]), .pin19(A[14]),
    .pin20(1'b1));
  LED led_1 (.in(_74382_1_pin14));
  LED led_2 (.in(_74382_1_pin13));
  LED led_3 (.in(_74382_1_pin14));
  LED led_4 (.in(_74382_2_pin14));
  LED led_5 (.in(_74382_2_pin14));
  LED led_6 (.in(_74382_3_pin14));
  LED led_7 (.in(_74382_3_pin14));
endmodule
