// Digital circuit 74382_single.dig as structural Verilog
module _74382_single (
  input  [3:0] A,
  input  [3:0] B,
  input  CnA,
  input  [2:0] Cmd,
  output [3:0] RES
);

  wire _74382_1_pin13, _74382_1_pin14;

  _74382 _74382_1 (
    .pin1(A[1]), .pin2(B[1]), .pin3(A[0]), .pin4(B[0]), .pin5(Cmd[0]), .pin6(Cmd[1]), .pin7(Cmd[2]),
    .pin8(RES[0]), .pin9(RES[1]), .pin10(1'b0), .pin11(RES[2]), .pin12(RES[3]), .pin13(_74382_1_pin13),
    .pin14(_74382_1_pin14), .pin15(CnA), .pin16(B[3]), .pin17(A[3]), .pin18(B[2]), .pin19(A[2]), .pin20(1'b1));
  LED led_1 (.in(_74382_1_pin14));
  LED led_2 (.in(_74382_1_pin13));

  // Other names for the same wires on the sheet: CMD_0 = Cmd[0]; CMD_1 = Cmd[1]; CMD_2 = Cmd[2]
endmodule
