// Digital circuit 74382_verilog.dig as structural Verilog
module _74382_verilog (
  input  [15:0] A,
  input  [15:0] B,
  input  CnA,
  input  [2:0] Cmd,
  output [16:0] Result
);

  wire u_alu_74382_2_cout, u_alu_74382_2_ovr, u_alu_74382_3_cout, u_alu_74382_3_ovr, u_alu_74382_4_ovr,
       u_alu_74382_cout, u_alu_74382_ovr;

  alu_74382 #(.applicationType("IVERILOG")) u_alu_74382 (
    .A(A[3:0]), .B(B[3:0]), .S(Cmd), .Cin(CnA), .Cout(u_alu_74382_cout), .Ovr(u_alu_74382_ovr),
    .F(Result[3:0]));
  alu_74382 #(.applicationType("IVERILOG")) u_alu_74382_2 (
    .A(A[7:4]), .B(B[7:4]), .S(Cmd), .Cin(u_alu_74382_cout), .Cout(u_alu_74382_2_cout),
    .Ovr(u_alu_74382_2_ovr), .F(Result[7:4]));
  alu_74382 #(.applicationType("IVERILOG")) u_alu_74382_3 (
    .A(A[11:8]), .B(B[11:8]), .S(Cmd), .Cin(u_alu_74382_2_cout), .Cout(u_alu_74382_3_cout),
    .Ovr(u_alu_74382_3_ovr), .F(Result[11:8]));
  alu_74382 #(.applicationType("IVERILOG")) u_alu_74382_4 (
    .A(A[15:12]), .B(B[15:12]), .S(Cmd), .Cin(u_alu_74382_3_cout), .Cout(Result[16]),
    .Ovr(u_alu_74382_4_ovr), .F(Result[15:12]));
  LED led_1 (.in(u_alu_74382_4_ovr));
  LED led_2 (.in(u_alu_74382_ovr));
  LED led_3 (.in(u_alu_74382_2_ovr));
  LED led_4 (.in(u_alu_74382_3_ovr));
endmodule

/* Code of alu_74382:
module alu_74382 (
    input [3:0] A, B,
    input [2:0] S,
    input Cin,
    output reg Cout, Ovr,
    output reg [3:0] F
);

always @(*)
    case (S)
        0: begin
            F = 4'b0000;
            Cout = 1'b0;
            Ovr = 1'b0;    
        end
        1: begin
            {Cout, F} = A - B + Cin;
            Ovr = ((A[3]^B[3])&(B[3]^F[3]));
            // Еще вариант реализации дополнения до двух
            // {Cout, F} = A + (~B) + Cin;
            //Ovr = (~A[3] & B[3] & ~F[3]) | (A[3] & ~B[3] & F[3]);
        end
        2: begin
            {Cout, F} = B - A + Cin;
            Ovr = ((A[3]^B[3])&(B[3]^F[3]));
            //  {Cout, F} = B + (~A) + Cin;
            //Ovr = (A[3] & ~B[3] & ~F[3]) | (~A[3] & B[3] & F[3]);
        end
        3: begin
            {Cout, F} = A + B + Cin;
            //OVR = (A[3] & B[3] & ~F[3]) | (~A[3] & ~B[3] & F[3]);
            Ovr = (!(A[3]^B[3]))&(B[3]^F[3]);
        end
        4: begin
            F = A ^ B;
            Ovr = (F == 4'b1111) ? Cin : 1'b0;
            Cout = Ovr;
        end
        5: begin
            F = A | B;
            Ovr = (F == 4'b1111) ? Cin : 1'b0;
            Cout = Ovr;
        end
        6: begin
            F = A & B;
            Ovr = (F == 4'b1111) ? Cin : 1'b0;
            Cout =  Ovr;
        end
        7: begin
            F = 4'b1111;
            Ovr = Cin;
            Cout = Ovr;
        end
    endcase

endmodule
*/
